# Fritzing sketch flip-bot (saved by Fritzing 0.9.3b)

parts:
  Part1 = NRF24L01+ Breakout Board
  SERVO1 = Tower Pro SG90 servo [part_number=101246]
  S1 = Pushbutton [package="[SMD]"]
  Part3 = Arduino Nano (Rev3.0) (ICSP)
  J1 = Piezo Speaker
  U1 = LIPO-110mAh [package=lipo-110]
  R1 = Trimmer Potentiometer [maximum_resistance=10kΩ package=THT]
  R2 = Trimmer Potentiometer [maximum_resistance=10kΩ package=THT]
  LED1 = RGB LED (com. cathode, rgb) [package="5 mm [THT]"]
  U2 = SWITCH_SPDT [package=kps-1290]

nets:
  GND: Part1.GND, SERVO1.GND, S1.Pin_3, S1.Pin_4, Part3.GND, J1.pin1, U1.-, R1.leg1, R2.leg1, LED1.common_cathode
  VCC: Part1.VCC, Part3.3V3
  N1: Part1.CE, Part3.D7
  N2: Part1.CS, Part3.D8
  N3: Part1.SCK, Part3.D13/SCK
  N4: Part1.MOSI, Part3.D11/MOSI
  N5: Part1.MISO, Part3.D12/MISO
  N6: SERVO1.Signal, Part3.D9
  +5V: SERVO1.+5V, Part3.5V, R1.leg2, R2.leg2
  N7: S1.Pin_1, Part3.D2
  N8: Part3.D3, LED1.blue_anode
  N9: Part3.D4, LED1.green_anode
  N10: Part3.D5, LED1.red_anode
  N11: Part3.D6, J1.pin2
  N12: Part3.VIN, U2.O
  N13: Part3.A1, R2.wiper
  N14: Part3.A0, R1.wiper
  N15: U1.+, U2.P

custom parts:
  Tower Pro SG90 servo: Original file by John De Cristofaro http://www.adafruit.com/products/1449 Adafruit Feedback Servo (Small) Edited by: e-radionica.com 28/9/2015
