# Fritzing sketch flipbot (saved by Fritzing 0.9.3b)

parts:
  Part1 = NRF24L01+ Breakout Board
  SERVO1 = Tower Pro SG90 servo [part_number=101246]
  VCC1 = Battery
  J1 = Piezo Speaker
  S1 = Pushbutton [package="[SMD]"]
  Part3 = Arduino Nano (Rev3.0) (ICSP)

nets:
  GND: Part1.GND, SERVO1.GND, VCC1.-, VCC1.+, J1.pin1, S1.Pin_3, S1.Pin_4, Part3.GND
  VCC: Part1.VCC, Part3.VIN
  N1: Part1.CE, Part3.D7
  N2: Part1.CS, Part3.D8
  N3: Part1.SCK, Part3.D13/SCK
  N4: Part1.MOSI, Part3.D11/MOSI
  N5: Part1.MISO, Part3.D12/MISO
  N6: SERVO1.Signal, Part3.D9
  +5V: SERVO1.+5V, Part3.5V
  N7: S1.Pin_1, Part3.D2

custom parts:
  Tower Pro SG90 servo: Original file by John De Cristofaro http://www.adafruit.com/products/1449 Adafruit Feedback Servo (Small) Edited by: e-radionica.com 28/9/2015
  Battery: Your standard 2x 18650 battery pack (7,4 Volts)
